// Digital circuit ProjetoMicroarquitetural.dig as structural Verilog
module ProjetoMicroarquitetural (
  input  clk
);

  wire add_1_p3, brg_1_p3, brg_1_p4, immext_1_p5, multiplexer_2_out, PC_p2, PC_p4, ula_1_p1, ula_1_p4,
       ula_1_p6, ula_1_p7;
  wire [1:0] PC_p3;
  wire [19:0] immext_1_p4;
  wire [31:0] add_1_p4, ula_1_p5;

  // REG PC: pin names not known; wires that end beside it: clk, PC_p2, PC_p3, PC_p4
  // ADD add_1: pin names not known; wires that end beside it: PC_p2, PC_p3, add_1_p3, add_1_p4[6:0]
  ROM #(.isProgramMemory("true")) MI (.A(PC_p3), .sel(PC_p4), .D(add_1_p4[0]));
  Multiplexer multiplexer_1 (.in_0(1'b0), .in_1(immext_1_p5), .out(add_1_p3));  // open: sel
  // IMMEXT immext_1: pin names not known; wires that end beside it: immext_1_p4[12:8], immext_1_p4[17:13], {add_1_p4[31:27], immext_1_p4[19:18]}, immext_1_p4, immext_1_p5
  // BRG brg_1: pin names not known; wires that end beside it: immext_1_p4[4:0], immext_1_p4[7:5], brg_1_p3, brg_1_p4
  Multiplexer multiplexer_2 (.sel(ula_1_p1), .in_0(brg_1_p4), .in_1(immext_1_p5), .out(multiplexer_2_out));
  // ULA ula_1: pin names not known; wires that end beside it: ula_1_p1, brg_1_p3, multiplexer_2_out, ula_1_p4, ula_1_p5, ula_1_p6, ula_1_p7
  LED led_1 (.in(ula_1_p4));
  RAMDualPort #(.AddrBits(5), .Bits(32)) MDD (
    .A(ula_1_p5[4:0]), .Din(ula_1_p5), .str(ula_1_p7), .C(clk), .ld(ula_1_p6));  // open: D
  // Pins of 5 and 32 bits meet at ula_1_p5
  // Pins of 1 and 32 bits meet at {add_1_p4[31:27], immext_1_p4, add_1_p4[6:0]}
  // Pins of 1 and 32 bits meet at 32'h4
endmodule
